// Digital circuit 2864.dig as structural Verilog
module _2864 (
  input  A0,
  input  A1,
  input  A2,
  input  A3,
  input  A4,
  input  A5,
  input  A6,
  input  A7,
  input  A8,
  input  A9,
  input  A10,
  input  A11,
  input  A12,
  input  nCE,
  input  nOE,
  input  nWE,
  input  VCC,
  input  GND,
  output I_O_0,
  output I_O_1,
  output I_O_2,
  output I_O_3,
  output I_O_4,
  output I_O_5,
  output I_O_6,
  output I_O_7
);

  wire nor_1_out;
  wire [7:0] eeprom_1_d;

  nor nor_1 (nor_1_out, nCE, ~nWE, nOE);  // NOr
  EEPROM #(.AddrBits(13), .Bits(8)) eeprom_1 (
    .A({A12, A11, A10, A9, A8, A7, A6, A5, A4, A3, A2, A1, A0}), .CS(~nCE), .WE(~nWE), .OE(~nOE),
    .D(eeprom_1_d));
  PowerSupply powersupply_1 (.VDD(VCC), .GND(GND));
  BusSplitter #(.Bits(8)) bussplitter_1 (
    .D(eeprom_1_d), .OE(nor_1_out), .D0(I_O_0), .D1(I_O_1), .D2(I_O_2), .D3(I_O_3), .D4(I_O_4), .D5(I_O_5),
    .D6(I_O_6), .D7(I_O_7));

  // Notes on the sheet:
  //   A0: pin 10
  //   A1: pin 9
  //   A2: pin 8
  //   A3: pin 7
  //   A4: pin 6
  //   A5: pin 5
  //   A6: pin 4
  //   A7: pin 3
  //   A8: pin 25
  //   A9: pin 24
  //   A10: pin 21
  //   A11: pin 23
  //   A12: pin 2
  //   nCE: pin 20, default 1
  //   nOE: pin 22, default 1
  //   nWE: pin 27, default 1
  //   I_O_0: pin 11
  //   I_O_1: pin 12
  //   I_O_2: pin 13
  //   I_O_3: pin 15
  //   I_O_4: pin 16
  //   I_O_5: pin 17
  //   I_O_6: pin 18
  //   I_O_7: pin 19
  //   VCC: pin 28, default 1
  //   GND: pin 14
  //   contents of eeprom_1 (hex, n*v repeats v):
  //   18*0,7e,81,a5,81,81,a5,99,81,81,7e,6*0,7e,ff,db,ff,ff,db,e7,ff,ff
  //   ,7e,8*0,6c,4*fe,7c,38,10,8*0,10,38,7c,fe,7c,38,10,8*0,18,3c,3c
  //   ,e7,e7,e7,18,18,3c,7*0,18,3c,7e,ff,ff,7e,18,18,3c,10*0,18,3c,3c
  //   ,18,6*0,6*ff,e7,c3,c3,e7,6*ff,5*0,3c,66,42,42,66,3c,5*0,5*ff,c3
  //   ,99,bd,bd,99,c3,5*ff,0,0,1e,6,e,1a,78,4*cc,78,6*0,3c,4*66,3c,18
  //   ,7e,18,18,6*0,3f,33,3f,4*30,70,f0,e0,6*0,7f,63,7f,4*63,67,e7,e6
  //   ,c0,6*0,18,18,db,3c,e7,3c,db,18,18,5*0,80,c0,e0,f0,f8,fe,f8,f0
  //   ,e0,c0,80,5*0,2,6,e,1e,3e,fe,3e,1e,e,6,2,6*0,18,3c,7e,18,18,18
  //   ,7e,3c,18,7*0,7*66,0,66,66,6*0,7f,db,db,db,7b,5*1b,5*0,7c,c6,60
  //   ,38,6c,c6,c6,6c,38,c,c6,7c,11*0,4*fe,6*0,18,3c,7e,18,18,18,7e
  //   ,3c,18,7e,6*0,18,3c,7e,7*18,6*0,7*18,7e,3c,18,9*0,18,c,fe,c,18
  //   ,11*0,30,60,fe,60,30,12*0,c0,c0,c0,fe,11*0,28,6c,fe,6c,28,10*0
  //   ,10,38,38,7c,7c,fe,fe,9*0,fe,fe,7c,7c,38,38,10,23*0,18,3c,3c,3c
  //   ,18,18,18,0,18,18,5*0,66,66,66,24,14*0,6c,6c,fe,6c,6c,6c,fe,6c,6c
  //   ,4*0,18,18,7c,c6,c2,c0,7c,6,6,86,c6,7c,18,18,6*0,c2,c6,c,18,30
  //   ,60,c6,86,6*0,38,6c,6c,38,76,dc,cc,cc,cc,76,5*0,30,30,30,60,13*0
  //   ,c,18,6*30,18,c,6*0,30,18,6*c,18,30,9*0,66,3c,ff,3c,66,11*0,18,18
  //   ,7e,18,18,15*0,18,18,18,30,10*0,fe,18*0,18,18,8*0,2,6,c,18,30
  //   ,60,c0,80,6*0,38,6c,c6,c6,d6,d6,c6,c6,6c,38,6*0,18,38,78,6*18
  //   ,7e,6*0,7c,c6,6,c,18,30,60,c0,c6,fe,6*0,7c,c6,6,6,3c,6,6,6,c6
  //   ,7c,6*0,c,1c,3c,6c,cc,fe,c,c,c,1e,6*0,fe,c0,c0,c0,fc,6,6,6,c6
  //   ,7c,6*0,38,60,c0,c0,fc,4*c6,7c,6*0,fe,c6,6,6,c,18,4*30,6*0,7c
  //   ,c6,c6,c6,7c,4*c6,7c,6*0,7c,c6,c6,c6,7e,6,6,6,c,78,8*0,18,18,0,0,0
  //   ,18,18,9*0,18,18,0,0,0,18,18,30,7*0,6,c,18,30,60,30,18,c,6,9*0
  //   ,7e,0,0,7e,10*0,60,30,18,c,6,c,18,30,60,6*0,7c,c6,c6,c,18,18,18
  //   ,0,18,18,7*0,7c,c6,c6,de,de,de,dc,c0,7c,6*0,10,38,6c,c6,c6,fe
  //   ,4*c6,6*0,fc,66,66,66,7c,4*66,fc,6*0,3c,66,c2,4*c0,c2,66,3c,6*0
  //   ,f8,6c,6*66,6c,f8,6*0,fe,66,62,68,78,68,60,62,66,fe,6*0,fe,66
  //   ,62,68,78,68,60,60,60,f0,6*0,3c,66,c2,c0,c0,de,c6,c6,66,3a,6*0
  //   ,4*c6,fe,5*c6,6*0,3c,8*18,3c,6*0,1e,5*c,cc,cc,cc,78,6*0,e6,66,66
  //   ,6c,78,78,6c,66,66,e6,6*0,f0,6*60,62,66,fe,6*0,c6,ee,fe,fe,d6
  //   ,5*c6,6*0,c6,e6,f6,fe,de,ce,4*c6,6*0,7c,8*c6,7c,6*0,fc,66,66,66
  //   ,7c,4*60,f0,6*0,7c,6*c6,d6,de,7c,c,e,4*0,fc,66,66,66,7c,6c,66,66,66
  //   ,e6,6*0,7c,c6,c6,60,38,c,6,c6,c6,7c,6*0,7e,7e,5a,6*18,3c,6*0,9*c6
  //   ,7c,6*0,7*c6,6c,38,10,6*0,4*c6,d6,d6,d6,fe,ee,6c,6*0,c6,c6,6c
  //   ,7c,38,38,7c,6c,c6,c6,6*0,4*66,3c,4*18,3c,6*0,fe,c6,86,c,18,30
  //   ,60,c2,c6,fe,6*0,3c,8*30,3c,7*0,80,c0,e0,70,38,1c,e,6,2,6*0,3c
  //   ,8*c,3c,4*0,10,38,6c,c6,25*0,ff,0,0,30,30,18,18*0,78,c,7c,cc,cc,cc
  //   ,76,6*0,e0,60,60,78,6c,4*66,7c,9*0,7c,c6,c0,c0,c0,c6,7c,6*0,1c
  //   ,c,c,3c,6c,4*cc,76,9*0,7c,c6,fe,c0,c0,c6,7c,6*0,38,6c,64,60,f0
  //   ,4*60,f0,9*0,76,5*cc,7c,c,cc,78,0,0,0,e0,60,60,6c,76,4*66,e6,6*0
  //   ,18,18,0,38,5*18,3c,6*0,6,6,0,e,6*6,66,66,3c,0,0,0,e0,60,60,66
  //   ,6c,78,78,6c,66,e6,6*0,38,8*18,3c,9*0,ec,fe,4*d6,c6,9*0,dc,6*66
  //   ,9*0,7c,5*c6,7c,9*0,dc,5*66,7c,60,60,f0,6*0,76,5*cc,7c,c,c,1e
  //   ,6*0,dc,76,66,60,60,60,f0,9*0,7c,c6,60,38,c,c6,7c,6*0,10,30,30
  //   ,fc,4*30,36,1c,9*0,6*cc,76,9*0,5*66,3c,18,9*0,c6,c6,d6,d6,d6,fe
  //   ,6c,9*0,c6,6c,38,38,38,6c,c6,9*0,6*c6,7e,6,c,f8,6*0,fe,cc,18,30
  //   ,60,c6,fe,6*0,e,18,18,18,70,4*18,e,6*0,4*18,0,5*18,6*0,70,18,18,18
  //   ,e,4*18,70,6*0,76,dc,16*0,10,38,6c,c6,c6,c6,fe,7*0,3c,66,c2,c0,c0,c0
  //   ,c2,66,3c,c,6,7c,4*0,cc,0,0,6*cc,76,5*0,c,18,30,0,7c,c6,fe,c0,c0
  //   ,c6,7c,5*0,10,38,6c,0,78,c,7c,cc,cc,cc,76,6*0,cc,0,0,78,c,7c,cc,cc,cc
  //   ,76,5*0,60,30,18,0,78,c,7c,cc,cc,cc,76,5*0,38,6c,38,0,78,c,7c
  //   ,cc,cc,cc,76,8*0,3c,66,60,60,66,3c,c,6,3c,4*0,10,38,6c,0,7c,c6
  //   ,fe,c0,c0,c6,7c,6*0,c6,0,0,7c,c6,fe,c0,c0,c6,7c,5*0,60,30,18,0
  //   ,7c,c6,fe,c0,c0,c6,7c,6*0,66,0,0,38,5*18,3c,5*0,18,3c,66,0,38
  //   ,5*18,3c,5*0,60,30,18,0,38,5*18,3c,5*0,c6,0,10,38,6c,c6,c6,fe
  //   ,c6,c6,c6,4*0,38,6c,38,0,38,6c,c6,c6,fe,c6,c6,c6,4*0,18,30,60
  //   ,0,fe,66,60,7c,60,60,66,fe,9*0,cc,76,36,7e,d8,d8,6e,6*0,3e,6c
  //   ,cc,cc,fe,4*cc,ce,5*0,10,38,6c,0,7c,5*c6,7c,6*0,c6,0,0,7c,5*c6
  //   ,7c,5*0,60,30,18,0,7c,5*c6,7c,5*0,30,78,cc,0,6*cc,76,5*0,60,30
  //   ,18,0,6*cc,76,6*0,c6,0,0,6*c6,7e,6,c,78,0,0,c6,0,7c,7*c6,7c,5*0
  //   ,c6,0,8*c6,7c,5*0,18,18,3c,66,60,60,60,66,3c,18,18,5*0,38,6c,64
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endmodule
