// Digital circuit 74245-RD.dig as structural Verilog
module _74245_RD (
  input  DIR,
  input  nOE,
  input  A8,
  input  A7,
  input  A6,
  input  A5,
  input  A4,
  input  A3,
  input  A2,
  input  A1,
  input  B8,
  input  B7,
  input  B6,
  input  B5,
  input  B4,
  input  B3,
  input  B2,
  input  B1,
  input  VCC,
  input  GND
);

  wire and_1_out, and_2_out;

  PowerSupply powersupply_1 (.VDD(VCC), .GND(GND));
  and and_1 (and_1_out, DIR, ~nOE);  // And
  assign B1 = and_1_out ? A1 : 1'bz;  // Driver driver_1
  assign B2 = and_1_out ? A2 : 1'bz;  // Driver driver_2
  assign B3 = and_1_out ? A3 : 1'bz;  // Driver driver_3
  assign B4 = and_1_out ? A4 : 1'bz;  // Driver driver_4
  assign B5 = and_1_out ? A5 : 1'bz;  // Driver driver_5
  assign B6 = and_1_out ? A6 : 1'bz;  // Driver driver_6
  assign B7 = and_1_out ? A7 : 1'bz;  // Driver driver_7
  assign B8 = and_1_out ? A8 : 1'bz;  // Driver driver_8
  and and_2 (and_2_out, ~nOE, ~DIR);  // And
  assign A1 = and_2_out ? B1 : 1'bz;  // Driver driver_9
  assign A2 = and_2_out ? B2 : 1'bz;  // Driver driver_10
  assign A3 = and_2_out ? B3 : 1'bz;  // Driver driver_11
  assign A4 = and_2_out ? B4 : 1'bz;  // Driver driver_12
  assign A5 = and_2_out ? B5 : 1'bz;  // Driver driver_13
  assign A6 = and_2_out ? B6 : 1'bz;  // Driver driver_14
  assign A7 = and_2_out ? B7 : 1'bz;  // Driver driver_15
  assign A8 = and_2_out ? B8 : 1'bz;  // Driver driver_16

  // Notes on the sheet:
  //   DIR: pin 1
  //   nOE: pin 19
  //   A8: pin 9
  //   A7: pin 8
  //   A6: pin 7
  //   A5: pin 6
  //   A4: pin 5
  //   A3: pin 4
  //   A2: pin 3
  //   A1: pin 2
  //   B8: pin 11
  //   B7: pin 12
  //   B6: pin 13
  //   B5: pin 14
  //   B4: pin 15
  //   B3: pin 16
  //   B2: pin 17
  //   B1: pin 18
  //   VCC: pin 20, default 1
  //   GND: pin 10
endmodule
