// Digital circuit i8088Test.dig as structural Verilog
module i8088Test (
  input  clk
);

  wire bussplitter_2_d0, bussplitter_2_d1, bussplitter_2_d2, bussplitter_2_d3, bussplitter_2_d4,
       bussplitter_2_d5, bussplitter_2_d6, bussplitter_2_d7, bussplitter_3_d0, bussplitter_3_d1,
       bussplitter_3_d2, bussplitter_3_d3, bussplitter_3_d4, bussplitter_3_d5, bussplitter_3_d6,
       bussplitter_3_d7, intel8088component_1_p20, intel8088component_1_p21, intel8088component_1_p22,
       intel8088component_1_p23, intel8088component_1_p24, intel8088component_1_p25,
       intel8088component_1_p26, intel8088component_1_p27, reset_1_out;
  wire [3:0] intel8088component_1_p11;
  wire [7:0] bussplitter_1_d, bussplitter_3_d, intel8088component_1_p19;
  wire [19:0] _74573_rd_3_q1;

  Reset #(.invertOutput("false")) reset_1 (.out(reset_1_out));
  // Intel8088Component intel8088component_1: pin names not known; wires that end beside it: 1'b0, 1'b0, clk, reset_1_out, 1'b1, 1'b0, 1'b0, intel8088component_1_p11[3], intel8088component_1_p11[2], intel8088component_1_p11[1], intel8088component_1_p11[0], intel8088component_1_p19[7], intel8088component_1_p19[6], intel8088component_1_p19[5], intel8088component_1_p19[4], intel8088component_1_p19[3], intel8088component_1_p19[2], intel8088component_1_p19[1], intel8088component_1_p19[0], intel8088component_1_p20, intel8088component_1_p21, intel8088component_1_p22, intel8088component_1_p23, intel8088component_1_p24, intel8088component_1_p25, intel8088component_1_p26, intel8088component_1_p27
  BusSplitter #(.Bits(8)) bussplitter_1 (
    .D(bussplitter_1_d), .D0(intel8088component_1_p27), .D1(intel8088component_1_p26),
    .D2(intel8088component_1_p25), .D3(intel8088component_1_p24), .D4(intel8088component_1_p23),
    .D5(intel8088component_1_p22), .D6(intel8088component_1_p21), .D7(intel8088component_1_p20));  // open: OE
  BusSplitter #(.Bits(8)) bussplitter_2 (
    .D(bussplitter_1_d), .D0(bussplitter_2_d0), .D1(bussplitter_2_d1), .D2(bussplitter_2_d2),
    .D3(bussplitter_2_d3), .D4(bussplitter_2_d4), .D5(bussplitter_2_d5), .D6(bussplitter_2_d6),
    .D7(bussplitter_2_d7));  // open: OE
  _74573_RD _74573_rd_1 (
    .Q0(_74573_rd_3_q1[16]), .Q1(_74573_rd_3_q1[17]), .Q2(_74573_rd_3_q1[18]), .Q3(_74573_rd_3_q1[19]),
    .D0(intel8088component_1_p11[0]), .D1(intel8088component_1_p11[1]), .D2(intel8088component_1_p11[2]),
    .D3(intel8088component_1_p11[3]), .VCC(1'b1), .GND(1'b0));  // open: Q4, Q5, Q6, Q7, nOC, D4, D5, D6, D7, C
  _74573_RD _74573_rd_2 (
    .Q0(_74573_rd_3_q1[8]), .Q1(_74573_rd_3_q1[9]), .Q2(_74573_rd_3_q1[10]), .Q3(_74573_rd_3_q1[11]),
    .Q4(_74573_rd_3_q1[12]), .Q5(_74573_rd_3_q1[13]), .Q6(_74573_rd_3_q1[14]), .Q7(_74573_rd_3_q1[15]),
    .D0(intel8088component_1_p19[0]), .D1(intel8088component_1_p19[1]), .D2(intel8088component_1_p19[2]),
    .D3(intel8088component_1_p19[3]), .D4(intel8088component_1_p19[4]), .D5(intel8088component_1_p19[5]),
    .D6(intel8088component_1_p19[6]), .D7(intel8088component_1_p19[7]), .VCC(1'b1), .GND(1'b0));  // open: nOC, C
  _74573_RD _74573_rd_3 (
    .Q0(_74573_rd_3_q1[0]), .Q1(_74573_rd_3_q1[1]), .Q2(_74573_rd_3_q1[2]), .Q3(_74573_rd_3_q1[3]),
    .Q4(_74573_rd_3_q1[4]), .Q5(_74573_rd_3_q1[5]), .Q6(_74573_rd_3_q1[6]), .Q7(_74573_rd_3_q1[7]),
    .D0(bussplitter_1_d[0]), .D1(bussplitter_1_d[1]), .D2(bussplitter_1_d[2]), .D3(bussplitter_1_d[3]),
    .D4(bussplitter_1_d[4]), .D5(bussplitter_1_d[5]), .D6(bussplitter_1_d[6]), .D7(bussplitter_1_d[7]),
    .VCC(1'b1), .GND(1'b0));  // open: nOC, C
  _74245_RD _74245_rd_1 (
    .A1(bussplitter_2_d0), .A2(bussplitter_2_d1), .A3(bussplitter_2_d2), .A4(bussplitter_2_d3),
    .A5(bussplitter_2_d4), .A6(bussplitter_2_d5), .A7(bussplitter_2_d6), .A8(bussplitter_2_d7),
    .B1(bussplitter_3_d0), .B2(bussplitter_3_d1), .B3(bussplitter_3_d2), .B4(bussplitter_3_d3),
    .B5(bussplitter_3_d4), .B6(bussplitter_3_d5), .B7(bussplitter_3_d6), .B8(bussplitter_3_d7), .VCC(1'b1),
    .GND(1'b0));  // open: nOE, DIR
  BusSplitter #(.Bits(8)) bussplitter_3 (
    .D(bussplitter_3_d), .D0(bussplitter_3_d0), .D1(bussplitter_3_d1), .D2(bussplitter_3_d2),
    .D3(bussplitter_3_d3), .D4(bussplitter_3_d4), .D5(bussplitter_3_d5), .D6(bussplitter_3_d6),
    .D7(bussplitter_3_d7));  // open: OE
  _2864 _2864_1 (
    .A0(_74573_rd_3_q1[0]), .A1(_74573_rd_3_q1[1]), .A2(_74573_rd_3_q1[2]), .A3(_74573_rd_3_q1[3]),
    .A4(_74573_rd_3_q1[4]), .A5(_74573_rd_3_q1[5]), .A6(_74573_rd_3_q1[6]), .A7(_74573_rd_3_q1[7]),
    .A8(_74573_rd_3_q1[8]), .A9(_74573_rd_3_q1[9]), .A10(_74573_rd_3_q1[10]), .A11(_74573_rd_3_q1[11]),
    .I_O_0(bussplitter_3_d[0]), .I_O_1(bussplitter_3_d[1]), .I_O_2(bussplitter_3_d[2]),
    .I_O_3(bussplitter_3_d[3]), .I_O_4(bussplitter_3_d[4]), .I_O_5(bussplitter_3_d[5]),
    .I_O_6(bussplitter_3_d[6]), .I_O_7(bussplitter_3_d[7]), .VCC(1'b1), .GND(1'b0));  // open: A12, nCE, nOE, nWE
  // Pins of 12 and 20 bits meet at _74573_rd_3_q1

  // Notes on the sheet:
  //   clk: Hz: 5
endmodule
