// Digital circuit i8288Test.dig as structural Verilog
module i8288Test (
  input  CLK,
  input  [2:0] Status,
  output DT_nR,
  output ALE,
  output DEN,
  output MCE_nPDEN,
  output out_7,
  output nMRDC,
  output out_9,
  output out_10,
  output out_11,
  output out_12,
  output out_13,
  output [3:0] BusT
);

  // Intel8288Component intel8288component_1: pin names not known; wires that end beside it: 1'b0, 1'b0, 1'b1, CLK, Status[2], Status[1], Status[0], DT_nR, ALE, DEN, MCE_nPDEN, out_7, nMRDC, out_9, out_10, out_11, out_12, out_13, BusT

  // Notes on the sheet:
  //   CLK: Hz: 4
  //   Status: default 7
endmodule

/* Test case System ~MRDC:
 CLK Status DT/~R ALE DEN MCE/~PDEN ~MRDC BusT
 0     7      1    0   0       0       1    0
 1     7      1    0   0       0       1    0

# T1
 0     5      1    1   0       1       1    1
 1     5      1    0   0       1       1    1

# T2
 0     5      0    0   0       0       0    2
 1     5      0    0   1       0       0    2

# T3
 0     7      0    0   1       0       0    3
 1     7      0    0   1       0       0    3

# T4
 0     7      0    0   0       0       1    4
 1     7      1    0   0       0       1    4

# T0
 0     7      1    0   0       0       1    0
 1     7      1    0   0       0       1    0
*/
